# Fritzing sketch robot1 (saved by Fritzing 0.9.3b)
circuit board: 8.46667cm x 5.64444cm
breadboards: 1

parts:
  Part2 = Rotoshield - Motor driver shield for Arduino
  M1 = DC Motor
  M2 = fc-51 [package=THT]
  Part3 = Bluetooth HC-05 Macho
  BAT1 = BC9VPC [package=bc9vpc]
  VCC1 = 4 x AAA Battery Mount
  M3 = DC Motor
  M4 = DC Motor
  M5 = DC Motor
  HC-SR04_Sensor_3 = HC-SR04 Ultrasonic Distance Sensor
  M6 = fc-51 [package=THT]
  M7 = fc-51 [package=THT]
  M8 = fc-51 [package=THT]
  Part1 = Arduino Uno (Rev3)
  Part5 = IMU Digital Combo Board 6DOF
  HC-SR04_Sensor_4 = HC-SR04 Ultrasonic Distance Sensor  # not connected

nets (from the breadboard view):
  N1: Part2.DIG_3, Part1.D3_PWM
  N2: Part2.DIG_4, Part1.D4
  N3: Part2.DIG_5, Part1.D5_PWM
  N4: Part2.DIG_6, Part1.D6_PWM
  N5: Part2.DIG_7, Part1.D7
  N6: Part2.DIG_8, Part1.D8
  N7: Part2.DIG_11, Part1.D11_PWM/MOSI
  N8: Part2.DIG_12, Part1.D12/MISO
  N9: Part2.M1-2, M3.pin_2
  N10: Part2.M1-1, M3.pin_1
  N11: Part2.M2-2, M1.pin_2
  N12: Part2.M2-1, M1.pin_1
  N13: Part2.M3-2, M5.pin_2
  N14: Part2.M3-1, M5.pin_1
  N15: Part2.M4-2, M4.pin_2
  N16: Part2.M4-1, M4.pin_1
  N17: Part2.VCC, VCC1.+
  N18: Part2.GND, VCC1.-
  N19: M2.pin1, Part1.A2
  GND: M2.pin2, Part3.GND, BAT1.V-, HC-SR04_Sensor_3.GND, M6.pin2, M7.pin2, M8.pin2, Part1.GND, Part5.GND
  VCC: M2.pin3, Part3.VCC, HC-SR04_Sensor_3.VCC, M6.pin3, M7.pin3, M8.pin3, Part1.5V, Part5.3.3V
  N20: Part3.TXD, Part1.D13/SCK
  N21: Part3.RXD, Part1.D2
  N22: BAT1.V+, Part1.VIN
  N23: HC-SR04_Sensor_3.TRIG, Part1.A1
  N24: HC-SR04_Sensor_3.ECHO, Part1.A0
  N25: M6.pin1, Part1.D10_PWM/SS
  N26: M7.pin1, Part1.D9_PWM
  N27: M8.pin1, Part1.A3
  N28: Part1.A4/SDA, Part5.SDA
  N29: Part1.A5/SCL, Part5.SCL
