# Fritzing sketch robot2 (saved by Fritzing 0.9.3b)
breadboards: 2

parts:
  Part2 = Rotoshield - Motor driver shield for Arduino
  M1 = DC Motor
  M2 = fc-51 [package=THT]
  Part3 = Bluetooth HC-05 Macho
  BAT1 = BC9VPC [package=bc9vpc]
  VCC1 = 4 x AAA Battery Mount
  M3 = DC Motor
  M4 = DC Motor
  M5 = DC Motor
  HC-SR04_Sensor_3 = HC-SR04 Ultrasonic Distance Sensor
  M6 = fc-51 [package=THT]
  M7 = fc-51 [package=THT]
  M8 = fc-51 [package=THT]
  IMU = IMU Digital Combo Board 6DOF
  HC-SR04_Sensor_4 = HC-SR04 Ultrasonic Distance Sensor
  Part6 = Arduino Due (Rev2b)
  HC-SR04_Sensor_5 = HC-SR04 Ultrasonic Distance Sensor
  Part8 = I2C level shifter bidirectional
  U1 = ESP8266 WiFi Module [part_number=ESP8266]

nets:
  N1: Part2.DIG_4, Part6.D4_PWM/SS1
  N2: Part2.DIG_5, Part6.D5_PWM
  N3: Part2.DIG_6, Part6.D6_PWM
  N4: Part2.DIG_7, Part6.D7_PWM
  N5: Part2.DIG_8, Part6.D8_PWM
  N6: Part2.DIG_10, Part6.D10_PWM/SS0
  N7: Part2.DIG_11, Part6.D11_PWM
  N8: Part2.DIG_12, Part6.D12_PWM
  N9: Part2.DIG_13, Part6.D13_PWM
  N10: Part2.GND, VCC1.-
  N11: Part2.VCC, VCC1.+
  N12: Part2.M1-2, M3.pin_2
  N13: Part2.M1-1, M3.pin_1
  N14: Part2.M2-2, M1.pin_2
  N15: Part2.M2-1, M1.pin_1
  N16: Part2.M3-2, M5.pin_2
  N17: Part2.M3-1, M5.pin_1
  N18: Part2.M4-2, M4.pin_2
  N19: Part2.M4-1, M4.pin_1
  N20: M2.pin1, Part6.D49
  GND: M2.pin2, Part3.GND, BAT1.V-, HC-SR04_Sensor_3.GND, M6.pin2, M7.pin2, M8.pin2, IMU.GND, HC-SR04_Sensor_4.GND, Part6.GND, HC-SR04_Sensor_5.GND, Part8.GND, U1.GND
  VCC: M2.pin3, Part3.VCC, HC-SR04_Sensor_3.VCC, M6.pin3, M7.pin3, M8.pin3, HC-SR04_Sensor_4.VCC, Part6.IOREF, HC-SR04_Sensor_5.VCC, Part8.LV, U1.3.3V
  N21: Part3.TXD, Part6.D51
  N22: Part3.RXD, Part6.D50
  N23: BAT1.V+, Part6.VIN
  N24: HC-SR04_Sensor_3.TRIG, Part6.A4
  N25: HC-SR04_Sensor_3.ECHO, Part8.HV1
  N26: M6.pin1, Part6.D46
  N27: M7.pin1, Part6.D47
  N28: M8.pin1, Part6.D48
  N29: IMU.SDA, Part6.SDA1
  N30: IMU.SCL, Part6.SCL1
  N31: HC-SR04_Sensor_4.TRIG, Part6.A2
  N32: HC-SR04_Sensor_4.ECHO, Part8.HV2
  N33: Part6.A0, HC-SR04_Sensor_5.TRIG
  N34: Part6.A1, Part8.LV3
  N35: Part6.A3, Part8.LV2
  N36: Part6.A5, Part8.LV1
  N37: Part6.D18/TX1, U1.RX
  N38: Part6.D19/RX1, U1.TX
  N39: Part6.5V, Part8.HV
  N40: HC-SR04_Sensor_5.ECHO, Part8.HV3
